# Fritzing sketch esp32 (saved by Fritzing 0.9.3b)

parts:
  M1 = >Wemos D1 R32
  U1 = Module 4 Relais 5V [package="Module 4 Relais 5V"]
  U2 = ESP32-38PinWide [part_number=ESP32-38PinWide]
  Mod1 = KY-035 Analog Magnetic Hall Sensor [package="Breakout board"]
  Componente1 = LCD1602-I2C
  BAT1 = BC9VPC [package=bc9vpc]
  C1 = Capacitor [package=cap-pth-small2]

nets:
  3V3: M1.3V3, Mod1.Vin
  5V: M1.5V, Componente1.VCC
  GND: M1.GND, Mod1.-, Componente1.GND, C1.2
  N1: M1.IO2, Mod1.S, C1.1
  N2: M1.SDA, Componente1.SDA
  N3: M1.SCL, Componente1.SCL
  N4: U1.VCC, U2.3.3
  GND_2: U1.GND, U2.GND, BAT1.V-
  N5: U1.IN1, U2.GPIO12
  N6: U1.IN2, U2.GPIO14
  N7: U1.IN3, U2.GPIO27
  N8: U1.IN4, U2.GPIO26
  N9: U1.K1-NO, U1.K2-NO
  N10: U2.VIN, BAT1.V+

notes:
  +24 V
  R1
  R2
  R3
  R4

custom parts:
  >Wemos D1 R32: Wemos D1 R32 - This board is used with dual-mode Wi-Fi and Bluetooth chips, which is safe, reliable, and scalable to a variety of applications. DC in 5V-12V, 1 analog input(3.2V max input), a Micro USB connection, Compatible with D1 R32=WiFi+bluetooth+UNO
  Module 4 Relais 5V: Module 4 Relais 5V 4x SPD-06VDC-SD-C
  ESP32-38PinWide: Generic 38-Pin ESP32 with wide format (only access to one side of pins on a breadboard) based on Stephen Lilley's HiLetgo ESP-WROOM-32 ESP32 ESP-32S Development Board.
  KY-035 Analog Magnetic Hall Sensor: KY-035 analog magnetic hall sensor is a module that reacts in the presence of a magnet. It can measure the polarity and relative strength of a magnetic field.
  LCD1602-I2C: A standard character display, usually with 2x16 characters. Comes in many colors with LCM1602 IIC attached.
